# Fritzing sketch dual_mpu6050_Schema (saved by Fritzing 0.9.5d)
breadboards: 2

parts:
  Part1 = Arduino Nano (Rev3.0)
  Part2 = InvenSense MPU6050
  Part3 = InvenSense MPU6050
  S1 = Pushbutton [package="[SMD]"]
  S2 = Pushbutton [package="[THT]"]
  S3 = Pushbutton [package="[THT]"]
  OLED_I2C1 = OLED 128x64 I2C Monochrome Display

nets:
  GND: Part1.GND, Part2.GND, Part2.AD0, Part3.GND, S1.Pin_3, S1.Pin_4, S2.Pin_3, S2.Pin_4, S3.Pin_3, S3.Pin_4, OLED_I2C1.GND
  N1: Part1.D2, S3.Pin_1, S3.Pin_2
  N2: Part1.D3, S2.Pin_1, S2.Pin_2
  N3: Part1.D4, S1.Pin_1, S1.Pin_2
  VCC: Part1.5V, Part2.VCC, Part3.VCC, Part3.AD0, OLED_I2C1.VDD
  N4: Part1.A5, Part2.SCL, Part3.SCL, OLED_I2C1.SCK
  N5: Part1.A4, Part2.SDA, Part3.SDA, OLED_I2C1.SDA
